// Logisim project Lab1.circ as structural Verilog: 1 circuit, main circuit main
module main (
  input  _1,
  input  _2,
  input  _3,
  input  _4,
  output D1,
  output D2
);

  wire nor_1_out, nor_2_out, nor_3_out, nor_4_out, nor_5_out, not_1_out, not_2_out, not_3_out, not_4_out,
       not_5_out, not_6_out;

  not not_1 (not_1_out, _2);
  nor nor_1 (nor_1_out, _1, _4);
  nor nor_2 (nor_2_out, _3, _4);
  not not_2 (not_2_out, _1);
  nor nor_3 (nor_3_out, not_2_out, not_3_out);
  not not_3 (not_3_out, _4);
  not not_4 (not_4_out, _2);
  nor nor_4 (nor_4_out, _3, not_5_out);
  not not_5 (not_5_out, _4);
  not not_6 (not_6_out, _3);
  nor nor_5 (nor_5_out, not_6_out, _4);
  nor nor_6 (D1, nor_1_out, not_1_out, nor_2_out, nor_3_out);
  nor nor_7 (D2, not_4_out, _1, nor_4_out, nor_5_out);
endmodule
