// Logisim project Lab2.circ as structural Verilog: 2 circuits, main circuit main
module main (
  input  A,
  input  S1,
  input  S0,
  input  B,
  input  C,
  input  D,
  output D1,
  output D2
);

  wire and_1_out, and_2_out, and_3_out, and_4_out, and_5_out, and_6_out, nA_out, nand_1_out, nand_2_out,
       nand_3_out, nand_4_out, nand_5_out, nand_6_out, nB_out, nC_out, nD_out, not_1_out, not_2_out;

  not nA (nA_out, A);
  not nB (nB_out, B);
  not nC (nC_out, C);
  not nD (nD_out, D);
  nand nand_1 (nand_1_out, nA_out, nB_out, nC_out, D);
  nand nand_2 (nand_2_out, A, nB_out, nD_out);
  nand nand_3 (nand_3_out, A, nB_out, nC_out, nD_out);
  nand nand_4 (nand_4_out, A, nB_out, C, D);
  nand nand_5 (nand_5_out, nand_1_out, nand_2_out);
  nand nand_6 (nand_6_out, nand_3_out, nand_4_out);
  not not_1 (not_1_out, S1);
  not not_2 (not_2_out, S0);
  and and_1 (and_1_out, not_2_out, not_1_out, nand_5_out);
  and and_2 (and_2_out, not_2_out, not_1_out, nand_6_out);
  and and_3 (and_3_out, not_1_out, S0, nand_5_out);
  and and_4 (and_4_out, not_2_out, not_1_out, nand_6_out);
  and and_5 (and_5_out, not_1_out, not_2_out, nand_5_out);
  and and_6 (and_6_out, not_2_out, S1, nand_6_out);
  or or_1 (D1, and_1_out, and_3_out, and_5_out);
  or or_2 (D2, and_2_out, and_4_out, and_6_out);
endmodule

module muxer (
  input  a,
  input  b
);

  wire a_prime_out, and_1_out, and_2_out, and_3_out, and_4_out, b_prime_out;

  not a_prime (a_prime_out, a);
  not b_prime (b_prime_out, b);
  and and_1 (and_1_out, a_prime_out, b_prime_out);
  and and_2 (and_2_out, b_prime_out, a);
  and and_3 (and_3_out, a_prime_out, b);
  and and_4 (and_4_out, a, b);
  // OR_Gate or_1 has open pins: in0=and_1_out, in1=and_2_out, in2=and_3_out, in3=and_4_out, out=open
endmodule
