// Logisim project Lab3.circ as structural Verilog: 1 circuit, main circuit main
module main (
  input  in_1,
  output out_2,
  output out_3
);

  wire and_1_out, and_2_out, and_3_out, and_4_out, clock_1_out, d_ff_1_q, d_ff_2_q, d_ff_3_q, d_ff_4_q,
       nand_1_out, nand_2_out;

  Clock clock_1 (.out(clock_1_out));
  D_Flip_Flop d_ff_1 (.clk(clock_1_out), .D(in_1), .Q(d_ff_1_q));  // open: Qn, preset, en, reset
  D_Flip_Flop d_ff_2 (.clk(clock_1_out), .D(d_ff_1_q), .Q(d_ff_2_q));  // open: Qn, preset, en, reset
  D_Flip_Flop d_ff_3 (.clk(clock_1_out), .D(d_ff_2_q), .Q(d_ff_3_q));  // open: Qn, preset, en, reset
  D_Flip_Flop d_ff_4 (.clk(clock_1_out), .D(d_ff_3_q), .Q(d_ff_4_q));  // open: Qn, preset, en, reset
  D_Flip_Flop d_ff_5 (.clk(clock_1_out), .D(d_ff_4_q), .Q(out_2));  // open: Qn, preset, en, reset
  and and_1 (and_1_out, d_ff_1_q, d_ff_3_q, out_2);
  nand nand_1 (nand_1_out, d_ff_2_q, d_ff_4_q);
  and and_2 (and_2_out, d_ff_1_q, d_ff_2_q);
  nand nand_2 (nand_2_out, d_ff_3_q, d_ff_4_q, out_2);
  and and_3 (and_3_out, and_1_out, nand_1_out);
  and and_4 (and_4_out, and_2_out, nand_2_out);
  or or_1 (out_3, and_3_out, and_4_out);
endmodule
